// Digital circuit 4-Bit AddSub.dig as structural Verilog
module _4_Bit_AddSub (
  input  [3:0] A,
  input  [3:0] B,
  input  K,
  output C_out,
  output [3:0] Sum
);

  wire _1_bit_full_adder_1_c_out, _1_bit_full_adder_2_c_out, _1_bit_full_adder_3_c_out, xor_1_out, xor_2_out,
       xor_3_out, xor_4_out;

  xor xor_1 (xor_1_out, K, B[0]);
  _1_Bit_Full_Adder _1_bit_full_adder_1 (
    .A(A[0]), .B(xor_1_out), .C_in(K), .Sum(Sum[0]), .C_out(_1_bit_full_adder_1_c_out));
  xor xor_2 (xor_2_out, K, B[1]);
  _1_Bit_Full_Adder _1_bit_full_adder_2 (
    .A(A[1]), .B(xor_2_out), .C_in(_1_bit_full_adder_1_c_out), .Sum(Sum[1]), .C_out(_1_bit_full_adder_2_c_out));
  xor xor_3 (xor_3_out, K, B[2]);
  _1_Bit_Full_Adder _1_bit_full_adder_3 (
    .A(A[2]), .B(xor_3_out), .C_in(_1_bit_full_adder_2_c_out), .Sum(Sum[2]), .C_out(_1_bit_full_adder_3_c_out));
  xor xor_4 (xor_4_out, K, B[3]);
  _1_Bit_Full_Adder _1_bit_full_adder_4 (
    .A(A[3]), .B(xor_4_out), .C_in(_1_bit_full_adder_3_c_out), .Sum(Sum[3]), .C_out(C_out));
endmodule
