// Digital circuit 4-Bit Adjusted ALU.dig as structural Verilog
module _4_Bit_Adjusted_ALU (
  input  [3:0] A,
  input  [3:0] B,
  input  [2:0] S_1___S_0___C_in,
  output [3:0] D,
  output C_out
);

  wire [3:0] multiplexer_1_out, not_1_out, not_2_out;

  Multiplexer #(.Selector_Bits(2), .Bits(4)) multiplexer_1 (
    .sel(S_1___S_0___C_in[2:1]), .in_0(B), .in_1(not_1_out), .in_2(4'b0000), .in_3(not_2_out),
    .out(multiplexer_1_out));
  assign not_1_out = ~B;  // Not not_1, 4 bits wide
  assign not_2_out = ~4'b0000;  // Not not_2, 4 bits wide
  _4_Bit_Full_Adder _4_bit_full_adder_1 (.A(A), .B(multiplexer_1_out), .K(S_1___S_0___C_in[0]), .C_out(C_out), .Sum(D));
  // Pins of 2 and 3 bits meet at S_1___S_0___C_in
endmodule
