// Digital circuit 4-Bit Full Adder.dig as structural Verilog
module _4_Bit_Full_Adder (
  input  [3:0] A,
  input  [3:0] B,
  input  K,
  output C_out,
  output [3:0] Sum
);

  wire _1_bit_full_adder_1_c_out, _1_bit_full_adder_2_c_out, _1_bit_full_adder_3_c_out;

  _1_Bit_Full_Adder _1_bit_full_adder_1 (.A(A[0]), .B(B[0]), .C_in(K), .Sum(Sum[0]), .C_out(_1_bit_full_adder_1_c_out));
  _1_Bit_Full_Adder _1_bit_full_adder_2 (
    .A(A[1]), .B(B[1]), .C_in(_1_bit_full_adder_1_c_out), .Sum(Sum[1]), .C_out(_1_bit_full_adder_2_c_out));
  _1_Bit_Full_Adder _1_bit_full_adder_3 (
    .A(A[2]), .B(B[2]), .C_in(_1_bit_full_adder_2_c_out), .Sum(Sum[2]), .C_out(_1_bit_full_adder_3_c_out));
  _1_Bit_Full_Adder _1_bit_full_adder_4 (
    .A(A[3]), .B(B[3]), .C_in(_1_bit_full_adder_3_c_out), .Sum(Sum[3]), .C_out(C_out));
endmodule
