// Digital circuit 5 Step FFDEWB.dig as structural Verilog
module _5_Step_FFDEWB (
  input  clk,
  output [4:0] States,
  output IF1,
  output IF2,
  output WB,
  output Inc
);

  D_FF #(.Default(1)) u_IF1 (.D(States[4]), .C(clk), .Q(IF1));  // open: nQ
  D_FF u_IF2 (.D(IF1), .C(clk), .Q(IF2));  // open: nQ
  D_FF Decode (.D(IF2), .C(clk), .Q(States[2]));  // open: nQ
  D_FF Execute (.D(States[2]), .C(clk), .Q(States[3]));  // open: nQ
  D_FF Write_Back (.D(States[3]), .C(clk), .Q(States[4]));  // open: nQ
  or or_1 (Inc, IF1, States[4]);

  assign States[1:0] = {IF2, IF1};
  assign WB = States[4];
endmodule
