// Digital circuit GPR.dig as structural Verilog
module GPR (
  input  [1:0] CSLI,
  input  [3:0] In,
  input  clk,
  output [3:0] Out
);

  wire [3:0] multiplexer_1_out;

  Multiplexer #(.Selector_Bits(2), .Bits(4)) multiplexer_1 (
    .sel(CSLI), .in_0(4'b0000), .in_1(In), .in_2(Out), .in_3(4'b1111), .out(multiplexer_1_out));
  D_FF d_ff_1 (.D(multiplexer_1_out[3]), .C(clk), .Q(Out[3]));  // open: nQ
  D_FF d_ff_2 (.D(multiplexer_1_out[2]), .C(clk), .Q(Out[2]));  // open: nQ
  D_FF d_ff_3 (.D(multiplexer_1_out[1]), .C(clk), .Q(Out[1]));  // open: nQ
  D_FF d_ff_4 (.D(multiplexer_1_out[0]), .C(clk), .Q(Out[0]));  // open: nQ

  // Notes on the sheet:
  //   CSLI: 0 = Clear
  //   1 = Store Input
  //   2 = Load
  //   3 = Set all bits equal to 1 (F)
  //   CLEAR/STORE/LOAD/INCREMENT
  //   In: Clear/Store/Load
endmodule
