// Digital circuit Instruction Memory.dig as structural Verilog
module Instruction_Memory (
  input  [1:0] IM_Control,
  input  clk,
  input  [1:0] IP_Control,
  input  [3:0] IM_Data_Input,
  output [3:0] Output
);

  wire [3:0] Instruction_Memory_output, Program_Counter_output;

  PC Program_Counter (.CSL(IP_Control), .Input(4'b0000), .Clock(clk), .Inc(4'b0001), .Output(Program_Counter_output));
  DRAM Instruction_Memory (
    .Address_Bus(Program_Counter_output), .Clock(clk), .Control_Bus(IM_Control), .Data_Bus(IM_Data_Input),
    .Output(Instruction_Memory_output));
  GPR Instruction_Register (.CSLI(2'b01), .In(Instruction_Memory_output), .clk(clk), .Out(Output));
endmodule
