// Digital circuit Register Files.dig as structural Verilog
module Register_Files (
  input  [7:0] CS,
  input  clk,
  input  [1:0] RR_1,
  input  [1:0] RR_2,
  input  [1:0] WR,
  input  [3:0] WD,
  output [3:0] RD_1,
  output [3:0] RD_2
);

  wire [3:0] demultiplexer_1_out_0, demultiplexer_1_out_1, demultiplexer_1_out_2, demultiplexer_1_out_3,
       R_0_out, R_1_out, R_2_out, R_3_out;

  Demultiplexer #(.Selector_Bits(2), .Bits(4)) demultiplexer_1 (
    .sel(WR), .in(WD), .out_0(demultiplexer_1_out_0), .out_1(demultiplexer_1_out_1),
    .out_2(demultiplexer_1_out_2), .out_3(demultiplexer_1_out_3));
  GPR R_0 (.CSLI(CS[1:0]), .In(demultiplexer_1_out_0), .clk(clk), .Out(R_0_out));
  GPR R_1 (.CSLI(CS[3:2]), .In(demultiplexer_1_out_1), .clk(clk), .Out(R_1_out));
  GPR R_2 (.CSLI(CS[5:4]), .In(demultiplexer_1_out_2), .clk(clk), .Out(R_2_out));
  GPR R_3 (.CSLI(CS[7:6]), .In(demultiplexer_1_out_3), .clk(clk), .Out(R_3_out));
  Multiplexer #(.Selector_Bits(2), .Bits(4)) multiplexer_1 (
    .sel(RR_1), .in_0(R_0_out), .in_1(R_1_out), .in_2(R_2_out), .in_3(R_3_out), .out(RD_1));
  Multiplexer #(.Selector_Bits(2), .Bits(4)) multiplexer_2 (
    .sel(RR_2), .in_0(R_0_out), .in_1(R_1_out), .in_2(R_2_out), .in_3(R_3_out), .out(RD_2));
endmodule
